# Fritzing sketch circuit (saved by Fritzing 0.9.3b)
perfboards: 1

parts:
  U1 = attiny85 [package=dip]
  U2 = Optocoupler [package=THT]
  SCR1 = SCR [package="TO220 [THT]"]
  R1 = Resistor [tolerance=±5% resistance=1k package="2512 [SMD]"]
  U3 = Mini-360 DC-DC Buck converter [package=THT]
  S2 = Pushbutton [package="[SMD]"]
  R2 = Resistor [tolerance=±5% resistance=10k package="2512 [SMD]"]
  U4 = TRANSISTOR_NPN_2 [package=to-92]
  JP1 = Header 2 [package=molex-1x2_lock]
  R3 = Resistor [tolerance=±5% resistance=10k package="2512 [SMD]"]
  R4 = Resistor [tolerance=±5% resistance=1k package="2512 [SMD]"]
  R5 = Resistor [tolerance=±5% resistance=1k package="2512 [SMD]"]
  R6 = Resistor [tolerance=±5% resistance=10k package="2512 [SMD]"]
  12V = Power Jack [package=power_jack_smd]
  JP2 = Header 2 [package=molex-1x2_lock]
  JP3 = Header 2 [package=molex-1x2_lock]
  D1 = Diode [package=diode-1n4001]
  Capacitor = Camdenboss CTB0158-2 [part_number=CTB0158-2 package=THT]
  300V = Camdenboss CTB0158-2 [part_number=CTB0158-2 package=THT]
  coil = Camdenboss CTB0158-2 [part_number=CTB0158-2 package=THT]
  JP4 = Header 4 [package=molex-1x4_lock]
  R7 = Resistor [tolerance=±5% resistance=1k package="2512 [SMD]"]
  Q1 = TRANSISTOR_PNP [package=to-92]
  JP5 = Header 2 [package=molex-1x2_lock]
  JP6 = Header 2 [package=molex-1x2_lock]

nets:
  N1: U1.Pin_2, JP4.2
  N2: U1.Pin_3, JP4.1
  GND: U1.Pin_4, U2.Pin_2, U2.Pin_4, SCR1.K, U3.OUT-, S2.Pin_1, S2.Pin_2, R2.Pin_0, R6.Pin_0, Capacitor.pin2, 300V.pin2, JP4.3, R7.Pin_1, JP5.2, JP6.2
  N3: U1.Pin_5, R5.Pin_0
  N4: U1.Pin_6, S2.Pin_3, S2.Pin_4, R3.Pin_0
  N5: U1.Pin_7, R1.Pin_0, R2.Pin_1
  5V: U1.Pin_8, U3.OUT+, R3.Pin_1, R4.Pin_0, JP4.4, Q1.E, JP5.1, JP6.1
  N6: U2.Pin_1, R5.Pin_1, R6.Pin_1
  N7: U2.Pin_5, R4.Pin_1, Q1.B
  N8: SCR1.A, D1.A, coil.pin2
  N9: SCR1.G, R7.Pin_0, Q1.C
  N10: R1.Pin_1, U4.B
  N11: U3.IN-, 12V.GND, JP2.2, JP3.2
  N12: U3.IN+, 12V.PWR, JP2.1, JP3.1
  N13: U4.E, JP1.2
  N14: U4.C, JP1.1
  N15: D1.C, Capacitor.pin1, 300V.pin1, coil.pin1

custom parts:
  SCR: Silicon Controlled Rectifier - TO220
  Mini-360 DC-DC Buck converter: Mini-360 DC-DC Buck converter. Tiny buck step down voltage converter, input voltage 4.75 to 23V output 1 to 17V adjustable. Available from ebay and the like.
  TRANSISTOR_NPN_2: Alternate TO-92 NPN BJT
